# Fritzing sketch Hardware (saved by Fritzing 0.9.0b)
circuit board: 8.46667cm x 5.64444cm

parts:
  LED1 = LED - 5mm [color="Green (555nm)" package="5 mm [THT]"]
  LED2 = LED - 5mm [color="Red (633nm)" package="5 mm [THT]"]
  Part1 = LilyPad Temperature Sensor
  Part2 = LilyTiny_LilyTwinkle
  Part3 = LilyPad Coin Cell Battery Holder

nets:
  N1: LED1.cathode, LED2.anode, Part2.1
  N2: LED1.anode, LED2.cathode, Part2.0
  N3: Part1.VCC, Part2.V+, Part3.+
  N4: Part1.GND, Part2.V-, Part3.-
  N5: Part1.VO, Part2.2

custom parts:
  LilyTiny_LilyTwinkle: LilyPad based on ATtiny85 part. LilyTiny and LilyTwinkle are different firmware versions; see the website for more information.
